// Digital circuit 1-bit-compare.dig as structural Verilog
module _1_bit_compare (
  input  A,
  input  B,
  output EQ,
  output G,
  output L
);

  wire and_2_out, and_3_out;

  and and_1 (L, ~A, B);  // And
  and and_2 (and_2_out, ~A, ~B);  // And
  and and_3 (and_3_out, A, B);
  and and_4 (G, A, ~B);  // And
  or or_1 (EQ, and_2_out, and_3_out);

  // Notes on the sheet:
  //   A: a input
  //   B: b input
  //   EQ: if the two inputs are equal
  //   G: high if b is greater than a
  //   L: a input is less than b input
endmodule
