// Digital circuit 1-bit-counter-with-load-clear.dig as structural Verilog
module _1_bit_counter_with_load_clear (
  input  LD,
  input  EN,
  input  D,
  input  CLR,
  input  CLK,
  output Q,
  output C
);

  wire and_1_out, and_2_out, or_1_out;

  and and_1 (and_1_out, CLK, D, LD);
  and and_2 (and_2_out, CLK, ~D, LD);  // And
  or or_1 (or_1_out, and_2_out, CLR);
  JK_FF_AS jk_ff_as_1 (.Set(and_1_out), .J(EN), .C(CLK), .K(EN), .Clr(or_1_out), .Q(Q));  // open: nQ
  and and_3 (C, EN, Q);

  // Notes on the sheet:
  //   LD: when high, counter loads synchronously
  //   EN: when 1, counting is enabled
  //   Q: counter value
  //   C: cascade count to next counter
  //   D: input value
  //   CLR: clear counter asynchronously
  //   CLK: clock input
endmodule
