// Digital circuit 1-bit-counter.dig as structural Verilog
module _1_bit_counter (
  input  LD,
  input  EN,
  input  D,
  input  CLR,
  input  CLK,
  output Q,
  output Q_NOT
);

  wire and_1_out, and_2_out, and_3_out, or_1_out;

  and and_1 (and_1_out, 1'b1, EN);
  and and_2 (and_2_out, D, CLK, LD);
  and and_3 (and_3_out, ~D, CLK, LD);  // And
  or or_1 (or_1_out, and_3_out, CLR);
  JK_FF_AS jk_ff_as_1 (.Set(and_2_out), .J(and_1_out), .C(CLK), .K(and_1_out), .Clr(or_1_out), .Q(Q), .nQ(Q_NOT));

  // Notes on the sheet:
  //   LD: load from input on next clock pulse
  //   EN: when 1, count up
  //   D: data preset
  //   CLR: clear the state on next clock cycle
  //   CLK: flip flop counts when signal goes high
  //   Q: data output
  //   Q_NOT: inverse of Q
endmodule
