// Digital circuit 1-bit-decrement.dig as structural Verilog
module _1_bit_decrement (
  input  C_IN,
  input  A,
  output D,
  output C_OUT
);

  wire and_1_out, and_2_out, xor_1_out;

  xor xor_1 (xor_1_out, 1'b1, A);
  and and_1 (and_1_out, 1'b1, A);
  xor xor_2 (D, xor_1_out, C_IN);
  and and_2 (and_2_out, C_IN, xor_1_out);
  or or_1 (C_OUT, and_2_out, and_1_out);

  // Notes on the sheet:
  //   C_IN: carry in bit
  //   A: input to decrement
  //   D: output of decrement
  //   C_OUT: carry out
endmodule
