// Digital circuit 1-bit-full-adder.dig as structural Verilog
module _1_bit_full_adder (
  input  C_IN,
  input  A_IN,
  input  B_IN,
  output C_OUT,
  output S_OUT
);

  wire and_1_out, and_2_out, xor_1_out;

  and and_1 (and_1_out, A_IN, B_IN);
  xor xor_1 (xor_1_out, A_IN, B_IN);
  and and_2 (and_2_out, xor_1_out, C_IN);
  xor xor_2 (S_OUT, xor_1_out, C_IN);
  or or_1 (C_OUT, and_1_out, and_2_out);

  // Notes on the sheet:
  //   C_OUT: carry out bit
  //   S_OUT: sum out
  //   C_IN: carry in bit
  //   A_IN: a input in
  //   B_IN: b input in
endmodule
