// Digital circuit 1s-complement-gen.dig as structural Verilog
module _1s_complement_gen (
  input  [7:0] IN,
  input  EN,
  output [7:0] OUT
);

  xor xor_1 (OUT[0], IN[0], EN);
  xor xor_2 (OUT[1], IN[1], EN);
  xor xor_3 (OUT[2], IN[2], EN);
  xor xor_4 (OUT[3], IN[3], EN);
  xor xor_5 (OUT[4], IN[4], EN);
  xor xor_6 (OUT[5], IN[5], EN);
  xor xor_7 (OUT[6], IN[6], EN);
  xor xor_8 (OUT[7], IN[7], EN);
  // Pins of 4 and 8 bits meet at IN

  // Notes on the sheet:
  //   IN: input data
  //   EN: when 1, 1's complement of input is generated
  //   OUT: data output
endmodule
