// Digital circuit 4-bit-compare-cascade.dig as structural Verilog
module _4_bit_compare_cascade (
  input  A0,
  input  A1,
  input  A2,
  input  A3,
  input  B0,
  input  B1,
  input  B2,
  input  B3,
  input  A__lt__B,
  input  A__eq__B,
  input  A__gt__B
);

  wire and_1_out, and_2_out, and_3_out, and_4_out, and_5_out, and_6_out, and_7_out, and_8_out, nand_1_out,
       nand_2_out, nand_3_out, nand_4_out, nor_1_out;

  nand nand_1 (nand_1_out, A3, B3);
  nand nand_2 (nand_2_out, A2, B2);
  nand nand_3 (nand_3_out, A1, B1);
  nand nand_4 (nand_4_out, A0, B0);
  and and_1 (and_1_out, A3, nand_1_out);
  and and_2 (and_2_out, nand_1_out, B3);
  and and_3 (and_3_out, A2, nand_2_out);
  and and_4 (and_4_out, nand_2_out, B2);
  and and_5 (and_5_out, A1, nand_3_out);
  and and_6 (and_6_out, nand_3_out, B1);
  and and_7 (and_7_out, A0, nand_4_out);
  and and_8 (and_8_out, nand_4_out, B0);
  // And and_9 has open pins: In_1=B3, In_2=nand_1_out, out=open
  nor nor_1 (nor_1_out, and_1_out, and_2_out);
  // NOr nor_2 has open pins: In_1=and_3_out, In_2=and_4_out, out=open
  // NOr nor_3 has open pins: In_1=and_5_out, In_2=and_6_out, out=open
  // NOr nor_4 has open pins: In_1=and_7_out, In_2=and_8_out, out=open
  // And and_10 has open pins: In_1=nand_1_out, In_2=A3, out=open
  // And and_11 has open pins: In_1=nor_1_out, In_2=nand_2_out, In_3=B2, out=open
  // And and_12 is placed but not wired
  // And and_13 is placed but not wired
  // And and_14 is placed but not wired

  // Notes on the sheet:
  //   A__lt__B: cascade
  //   A__eq__B: cascade
  //   A__gt__B: cascade
endmodule
