// Digital circuit 4-bit-counter-with-load-clear.dig as structural Verilog
module _4_bit_counter_with_load_clear (
  input  LD,
  input  EN,
  input  [3:0] D_IN,
  input  CLR,
  input  CLK,
  output [3:0] D_OUT,
  output C
);

  wire _1_bit_counter_with_load_clear_1_c, _1_bit_counter_with_load_clear_2_c,
       _1_bit_counter_with_load_clear_3_c;

  _1_bit_counter_with_load_clear _1_bit_counter_with_load_clear_1 (
    .LD(LD), .EN(EN), .D(D_IN[0]), .CLR(CLR), .CLK(CLK), .Q(D_OUT[0]), .C(_1_bit_counter_with_load_clear_1_c));
  _1_bit_counter_with_load_clear _1_bit_counter_with_load_clear_2 (
    .LD(LD), .EN(_1_bit_counter_with_load_clear_1_c), .D(D_IN[1]), .CLR(CLR), .CLK(CLK), .Q(D_OUT[1]),
    .C(_1_bit_counter_with_load_clear_2_c));
  _1_bit_counter_with_load_clear _1_bit_counter_with_load_clear_3 (
    .LD(LD), .EN(_1_bit_counter_with_load_clear_2_c), .D(D_IN[2]), .CLR(CLR), .CLK(CLK), .Q(D_OUT[2]),
    .C(_1_bit_counter_with_load_clear_3_c));
  _1_bit_counter_with_load_clear _1_bit_counter_with_load_clear_4 (
    .LD(LD), .EN(_1_bit_counter_with_load_clear_3_c), .D(D_IN[3]), .CLR(CLR), .CLK(CLK), .Q(D_OUT[3]), .C(C));

  // Notes on the sheet:
  //   LD: when 1, counter loads from D
  //   EN: when 1, counter will increment on clock pulse
  //   D_IN: data input
  //   CLR: when 1, counter clears asynchronously
  //   CLK: clock input
  //   D_OUT: data output
  //   C: cascade to additional counters
endmodule
