// Digital circuit 4-bit-counter.dig as structural Verilog
module _4_bit_counter (
  input  LD,
  input  EN,
  input  [3:0] D_IN,
  input  CLR,
  input  CLK,
  output [3:0] D_OUT
);

  wire and_1_out, and_2_out;

  and and_1 (and_1_out, D_OUT[1], D_OUT[0]);
  and and_2 (and_2_out, D_OUT[1], D_OUT[0], D_OUT[2]);
  _1_bit_counter _1_bit_counter_1 (.LD(LD), .EN(EN), .D(D_IN[0]), .CLR(CLR), .CLK(CLK), .Q(D_OUT[0]));  // open: Q_NOT
  _1_bit_counter _1_bit_counter_2 (
    .LD(LD), .EN(D_OUT[0]), .D(D_IN[1]), .CLR(CLR), .CLK(CLK), .Q(D_OUT[1]));  // open: Q_NOT
  _1_bit_counter _1_bit_counter_3 (
    .LD(LD), .EN(and_1_out), .D(D_IN[2]), .CLR(CLR), .CLK(CLK), .Q(D_OUT[2]));  // open: Q_NOT
  _1_bit_counter _1_bit_counter_4 (
    .LD(LD), .EN(and_2_out), .D(D_IN[3]), .CLR(CLR), .CLK(CLK), .Q(D_OUT[3]));  // open: Q_NOT

  // Notes on the sheet:
  //   LD: when 1, counter loads from D
  //   EN: when 1, counter will increment on clock pulse
  //   D_IN: data input
  //   CLR: when 1, counter clears asynchronously
  //   CLK: clock input
  //   D_OUT: data output
endmodule
