// Digital circuit 4-bit-decrement.dig as structural Verilog
module _4_bit_decrement (
  input  [3:0] A,
  input  C_IN,
  output [3:0] D,
  output C_OUT
);

  wire _1_bit_decrement_1_c_out, _1_bit_decrement_2_c_out, _1_bit_decrement_3_c_out;

  _1_bit_decrement _1_bit_decrement_1 (.C_IN(C_IN), .A(A[0]), .D(D[0]), .C_OUT(_1_bit_decrement_1_c_out));
  _1_bit_decrement _1_bit_decrement_2 (
    .C_IN(_1_bit_decrement_1_c_out), .A(A[1]), .D(D[1]), .C_OUT(_1_bit_decrement_2_c_out));
  _1_bit_decrement _1_bit_decrement_3 (
    .C_IN(_1_bit_decrement_2_c_out), .A(A[2]), .D(D[2]), .C_OUT(_1_bit_decrement_3_c_out));
  _1_bit_decrement _1_bit_decrement_4 (.C_IN(_1_bit_decrement_3_c_out), .A(A[3]), .D(D[3]), .C_OUT(C_OUT));

  // Notes on the sheet:
  //   A: data input
  //   D: data output
  //   C_IN: carry in bit
  //   C_OUT: carry out bit
endmodule
