// Digital circuit 4-bit-full-adder.dig as structural Verilog
module _4_bit_full_adder (
  input  [3:0] A_IN,
  input  [3:0] B_IN,
  input  C_IN,
  output [3:0] S_OUT,
  output C_OUT
);

  wire _1_bit_full_adder_1_c_out, _1_bit_full_adder_2_c_out, _1_bit_full_adder_3_c_out;

  _1_bit_full_adder _1_bit_full_adder_1 (
    .C_IN(C_IN), .A_IN(A_IN[0]), .B_IN(B_IN[0]), .C_OUT(_1_bit_full_adder_1_c_out), .S_OUT(S_OUT[0]));
  _1_bit_full_adder _1_bit_full_adder_2 (
    .C_IN(_1_bit_full_adder_1_c_out), .A_IN(A_IN[1]), .B_IN(B_IN[1]), .C_OUT(_1_bit_full_adder_2_c_out),
    .S_OUT(S_OUT[1]));
  _1_bit_full_adder _1_bit_full_adder_3 (
    .C_IN(_1_bit_full_adder_2_c_out), .A_IN(A_IN[2]), .B_IN(B_IN[2]), .C_OUT(_1_bit_full_adder_3_c_out),
    .S_OUT(S_OUT[2]));
  _1_bit_full_adder _1_bit_full_adder_4 (
    .C_IN(_1_bit_full_adder_3_c_out), .A_IN(A_IN[3]), .B_IN(B_IN[3]), .C_OUT(C_OUT), .S_OUT(S_OUT[3]));

  // Notes on the sheet:
  //   A_IN: a inputs in
  //   B_IN: b inputs in
  //   C_IN: carry in bit
  //   S_OUT: summation of the two inputs
  //   C_OUT: carry bit out
endmodule
