// Digital circuit 4-bit-register.dig as structural Verilog
module _4_bit_register (
  input  [3:0] D,
  input  LD,
  input  CLK,
  input  CLR,
  output [3:0] Q
);

  buffered_d_flipflop buffered_d_flipflop_1 (.D(D[0]), .LOAD(LD), .CLK(CLK), .CLR(CLR), .Q(Q[0]));
  buffered_d_flipflop buffered_d_flipflop_2 (.D(D[1]), .LOAD(LD), .CLK(CLK), .CLR(CLR), .Q(Q[1]));
  buffered_d_flipflop buffered_d_flipflop_3 (.D(D[2]), .LOAD(LD), .CLK(CLK), .CLR(CLR), .Q(Q[2]));
  buffered_d_flipflop buffered_d_flipflop_4 (.D(D[3]), .LOAD(LD), .CLK(CLK), .CLR(CLR), .Q(Q[3]));
  // Pins of 1 and 4 bits meet at Q

  // Notes on the sheet:
  //   D: data in
  //   LD: data is loaded from input on next clock cycle when high
  //   CLK: clock input
  //   CLR: clears register async
  //   Q: register value out
endmodule
