// Digital circuit 8-bit-alu.dig as structural Verilog
module _8_bit_alu (
  input  [7:0] A_IN,
  input  SO,
  input  SUB,
  input  [7:0] B_IN,
  output [7:0] S_OUT,
  output CARRY,
  output ZR,
  output GT,
  output EQ,
  output LT
);

  wire _4_bit_full_adder_1_c_out;
  wire [3:0] _4_bit_full_adder_1_s_out, _4_bit_full_adder_2_s_out;
  wire [7:0] _1s_complement_gen_1_p3;

  // _1s_complement_gen _1s_complement_gen_1: pin names not known; wires that end beside it: B_IN, SUB, _1s_complement_gen_1_p3
  _4_bit_full_adder _4_bit_full_adder_1 (
    .A_IN(A_IN[3:0]), .B_IN(_1s_complement_gen_1_p3[3:0]), .C_IN(SUB), .S_OUT(_4_bit_full_adder_1_s_out),
    .C_OUT(_4_bit_full_adder_1_c_out));
  _4_bit_full_adder _4_bit_full_adder_2 (
    .A_IN(A_IN[7:4]), .B_IN(_1s_complement_gen_1_p3[7:4]), .C_IN(_4_bit_full_adder_1_c_out),
    .S_OUT(_4_bit_full_adder_2_s_out), .C_OUT(CARRY));
  Comparator #(.Bits(8)) comparator_1 (.a(A_IN), .b(B_IN), .gt(GT), .eq(EQ), .lt(LT));
  assign S_OUT = SO ? {_4_bit_full_adder_2_s_out, _4_bit_full_adder_1_s_out} : 8'bz;  // Driver driver_1
  nor nor_1 (ZR, _4_bit_full_adder_1_s_out[0], _4_bit_full_adder_1_s_out[1], _4_bit_full_adder_1_s_out[2], _4_bit_full_adder_1_s_out[3], _4_bit_full_adder_2_s_out[0], _4_bit_full_adder_2_s_out[1], _4_bit_full_adder_2_s_out[2], _4_bit_full_adder_2_s_out[3]);

  // Notes on the sheet:
  //   A_IN: a input
  //   SO: when 1, places the arithmatic result on the output line
  //   SUB: when 1, alu subtracts rather than adds
  //   B_IN: b input
  //   S_OUT: arithmetic result out
  //   CARRY: set if the result of the arithmetic carries
  //   ZR: result of computation is zero when set
  //   GT: if a is greater than b, this is high
  //   EQ: if a and b are equal, this line is high
  //   LT: if a is less than b, this output is high
endmodule
