// Digital circuit 8-bit-counter.dig as structural Verilog
module _8_bit_counter (
  input  LD,
  input  EN,
  input  [7:0] D_IN,
  input  CLR,
  input  CLK,
  output [7:0] D_OUT
);

  wire and_1_out, and_2_out, and_3_out, and_4_out, and_5_out, and_6_out, and_7_out;

  and and_1 (and_1_out, EN, D_OUT[0]);
  and and_2 (and_2_out, EN, D_OUT[0], D_OUT[1]);
  and and_3 (and_3_out, EN, D_OUT[0], D_OUT[1], D_OUT[2]);
  and and_4 (and_4_out, EN, D_OUT[0], D_OUT[1], D_OUT[2], D_OUT[3]);
  and and_5 (and_5_out, EN, D_OUT[0], D_OUT[1], D_OUT[2], D_OUT[3], D_OUT[4]);
  and and_6 (and_6_out, EN, D_OUT[0], D_OUT[1], D_OUT[2], D_OUT[3], D_OUT[4], D_OUT[5]);
  and and_7 (and_7_out, EN, D_OUT[0], D_OUT[1], D_OUT[2], D_OUT[3], D_OUT[4], D_OUT[5], D_OUT[6]);
  _1_bit_counter _1_bit_counter_1 (.LD(LD), .EN(EN), .D(D_IN[0]), .CLR(CLR), .CLK(CLK), .Q(D_OUT[0]));  // open: Q_NOT
  _1_bit_counter _1_bit_counter_2 (
    .LD(LD), .EN(and_1_out), .D(D_IN[1]), .CLR(CLR), .CLK(CLK), .Q(D_OUT[1]));  // open: Q_NOT
  _1_bit_counter _1_bit_counter_3 (
    .LD(LD), .EN(and_2_out), .D(D_IN[2]), .CLR(CLR), .CLK(CLK), .Q(D_OUT[2]));  // open: Q_NOT
  _1_bit_counter _1_bit_counter_4 (
    .LD(LD), .EN(and_3_out), .D(D_IN[3]), .CLR(CLR), .CLK(CLK), .Q(D_OUT[3]));  // open: Q_NOT
  _1_bit_counter _1_bit_counter_5 (
    .LD(LD), .EN(and_4_out), .D(D_IN[4]), .CLR(CLR), .CLK(CLK), .Q(D_OUT[4]));  // open: Q_NOT
  _1_bit_counter _1_bit_counter_6 (
    .LD(LD), .EN(and_5_out), .D(D_IN[5]), .CLR(CLR), .CLK(CLK), .Q(D_OUT[5]));  // open: Q_NOT
  _1_bit_counter _1_bit_counter_7 (
    .LD(LD), .EN(and_6_out), .D(D_IN[6]), .CLR(CLR), .CLK(CLK), .Q(D_OUT[6]));  // open: Q_NOT
  _1_bit_counter _1_bit_counter_8 (
    .LD(LD), .EN(and_7_out), .D(D_IN[7]), .CLR(CLR), .CLK(CLK), .Q(D_OUT[7]));  // open: Q_NOT

  // Notes on the sheet:
  //   LD: when 1, counter loads from D
  //   EN: when 1, counter will increment on clock pulse
  //   D_IN: data input
  //   CLR: when 1, counter clears asynchronously
  //   CLK: clock input
  //   D_OUT: data output
endmodule
