// Digital circuit 8-bit-decrement.dig as structural Verilog
module _8_bit_decrement (
  input  [7:0] A,
  input  C_IN,
  output [7:0] D,
  output C_OUT
);

  wire _4_bit_decrement_1_c_out;

  _4_bit_decrement _4_bit_decrement_1 (.A(A[3:0]), .C_IN(C_IN), .D(D[3:0]), .C_OUT(_4_bit_decrement_1_c_out));
  _4_bit_decrement _4_bit_decrement_2 (.A(A[7:4]), .C_IN(_4_bit_decrement_1_c_out), .D(D[7:4]), .C_OUT(C_OUT));

  // Notes on the sheet:
  //   A: data input
  //   D: output bits
  //   C_OUT: carry out bit
  //   C_IN: carry in bit
endmodule
