// Digital circuit 8-bit-memory-unit.dig as structural Verilog
module _8_bit_memory_unit (
  input  CLK,
  input  MAL,
  input  [7:0] D_IN,
  input  MEL,
  input  MEE,
  input  CLR,
  output [7:0] D_OUT
);

  wire [7:0] _8_bit_register_1_qd;

  _8_bit_register _8_bit_register_1 (
    .D(D_IN), .ST(MAL), .EN(1'b0), .CLK(CLK), .CLR(CLR), .QD(_8_bit_register_1_qd));  // open: Q
  assign D_OUT = MEL ? D_IN : 8'bz;  // Driver driver_1
  RAMSinglePort #(.AddrBits(8), .isProgramMemory("true"), .Bits(8)) RAM (
    .A(_8_bit_register_1_qd), .str(MEL), .C(CLK), .ld(MEE), .D(D_OUT));

  // Notes on the sheet:
  //   CLK: clock input
  //   MAL: when high, memory address will be stored in MAR on clock pulse
  //   D_IN: data input
  //   MEL: when high, stores the data on the bus at the memory address stored in the MAR
  //   MEE: place a word of data on the bus from memory
  //   D_OUT: data bus out
  //   CLR: clear MAR async
endmodule
