// Digital circuit 8-bit-register.dig as structural Verilog
module _8_bit_register (
  input  [7:0] D,
  input  ST,
  input  EN,
  input  CLK,
  input  CLR,
  output [7:0] QD,
  output [7:0] Q
);

  buffered_d_flipflop buffered_d_flipflop_1 (.D(D[0]), .LOAD(ST), .CLK(CLK), .CLR(CLR), .Q(QD[0]));
  buffered_d_flipflop buffered_d_flipflop_2 (.D(D[1]), .LOAD(ST), .CLK(CLK), .CLR(CLR), .Q(QD[1]));
  buffered_d_flipflop buffered_d_flipflop_3 (.D(D[2]), .LOAD(ST), .CLK(CLK), .CLR(CLR), .Q(QD[2]));
  buffered_d_flipflop buffered_d_flipflop_4 (.D(D[3]), .LOAD(ST), .CLK(CLK), .CLR(CLR), .Q(QD[3]));
  buffered_d_flipflop buffered_d_flipflop_5 (.D(D[4]), .LOAD(ST), .CLK(CLK), .CLR(CLR), .Q(QD[4]));
  buffered_d_flipflop buffered_d_flipflop_6 (.D(D[5]), .LOAD(ST), .CLK(CLK), .CLR(CLR), .Q(QD[5]));
  buffered_d_flipflop buffered_d_flipflop_7 (.D(D[6]), .LOAD(ST), .CLK(CLK), .CLR(CLR), .Q(QD[6]));
  buffered_d_flipflop buffered_d_flipflop_8 (.D(D[7]), .LOAD(ST), .CLK(CLK), .CLR(CLR), .Q(QD[7]));
  assign Q = EN ? QD : 8'bz;  // Driver driver_1

  // Notes on the sheet:
  //   D: data input
  //   ST: when 1, data stores from input on rising edge of clock
  //   EN: enable output
  //   QD: non-buffered output (for lcd display)
  //   Q: buffered data output
  //   CLK: clock input
  //   CLR: clear register async
endmodule
