// Digital circuit alu.dig as structural Verilog
module alu (
  input  [3:0] DATA_IN,
  input  A_LD,
  input  B_LD,
  input  [1:0] OP,
  input  A_EN,
  output [3:0] DATA_OUT
);

  wire decoder_1_out_0, decoder_1_out_1, not_1_out;
  wire [3:0] A_REG_q, ADD_s, B_REG_q, SUB_s;

  Register #(.Bits(4)) A_REG (.D(DATA_IN), .C(A_LD), .en(1'b1), .Q(A_REG_q));
  not not_1 (not_1_out, 1'b1);
  Register #(.Bits(4)) B_REG (.D(DATA_IN), .C(B_LD), .en(1'b1), .Q(B_REG_q));
  assign DATA_OUT = A_EN ? A_REG_q : 4'bz;  // Driver driver_1
  Add #(.Bits(4)) ADD (.a(A_REG_q), .b(B_REG_q), .c_i(not_1_out), .s(ADD_s));  // open: c_o
  Sub #(.Bits(4)) SUB (.a(A_REG_q), .b(B_REG_q), .c_i(not_1_out), .s(SUB_s));  // open: c_o
  Comparator #(.Bits(4)) CMP_UNSIGNED (.a(A_REG_q), .b(B_REG_q));  // open: gt, eq, lt
  Decoder #(.Selector_Bits(2)) decoder_1 (
    .sel(OP), .out_0(decoder_1_out_0), .out_1(decoder_1_out_1));  // open: out_2, out_3
  assign DATA_OUT = decoder_1_out_0 ? ADD_s : 4'bz;  // Driver driver_2
  assign DATA_OUT = decoder_1_out_1 ? SUB_s : 4'bz;  // Driver driver_3

  // Notes on the sheet:
  //   DATA_IN: Data bus input
  //   A_LD: Load the accumulator
  //   B_LD: Load the data register
  //   DATA_OUT: Data bus out
  //   OP: ALU operation flags
  //   A_EN: Enable accumulator on the bus
endmodule
