// Digital circuit buffered-d-flipflop.dig as structural Verilog
module buffered_d_flipflop (
  input  D,
  input  LOAD,
  input  CLK,
  input  CLR,
  output Q
);

  wire and_1_out, and_2_out, not_1_out, or_1_out;

  not not_1 (not_1_out, LOAD);
  and and_1 (and_1_out, Q, not_1_out);
  and and_2 (and_2_out, D, LOAD);
  or or_1 (or_1_out, and_1_out, and_2_out);
  D_FF_AS d_ff_as_1 (.Set(1'b0), .D(or_1_out), .C(CLK), .Clr(CLR), .Q(Q));  // open: nQ

  // Notes on the sheet:
  //   D: data in
  //   Q: data out
  //   LOAD: load data to the register when 1
  //   CLK: clock pulse in. data stores on rising edge
  //   CLR: clears the flip flop asynchronously
endmodule
