// Digital circuit cpu.dig as structural Verilog
module cpu (
  input  SYSCLK
);

  wire _8_bit_alu_1_carry, _8_bit_alu_1_zr, and_1_out, and_2_out, and_3_out, instruction_decoder_1_ai,
       instruction_decoder_1_ao, instruction_decoder_1_bi, instruction_decoder_1_bo,
       instruction_decoder_1_in, instruction_decoder_1_iri, instruction_decoder_1_mai,
       instruction_decoder_1_mi, instruction_decoder_1_mo, instruction_decoder_1_out,
       instruction_decoder_1_pcc, instruction_decoder_1_pce, instruction_decoder_1_pop,
       instruction_decoder_1_so, instruction_decoder_1_spc, instruction_decoder_1_spi,
       instruction_decoder_1_spo, instruction_decoder_1_sub, ON_ovf, POWER_out, RESET_out;
  wire [3:0] A_REG_qd, A_REG_qd_2, B_REG_qd, B_REG_qd_2, instruction_decoder_1_s;
  wire [7:0] _8_bit_memory_unit_1_d_out, instruction_decoder_1_ird, program_counter_1_q, stack_register_1_qd;
  wire [15:8] keyboard_1_d;

  Button POWER (.out(POWER_out));
  Button RESET (.out(RESET_out));
  Seven_Seg_Hex seven_seg_hex_1 (.d(instruction_decoder_1_ird[7:4]), .dp(1'b0));
  Counter ON (.en(1'b1), .C(POWER_out), .clr(1'b0), .ovf(ON_ovf));  // open: out
  Seven_Seg_Hex seven_seg_hex_2 (.d(instruction_decoder_1_ird[3:0]), .dp(1'b0));
  and and_1 (and_1_out, SYSCLK, ON_ovf);
  _8_bit_memory_unit _8_bit_memory_unit_1 (
    .CLK(and_1_out), .MAL(instruction_decoder_1_mai), .D_IN(_8_bit_memory_unit_1_d_out),
    .MEL(instruction_decoder_1_mi), .MEE(instruction_decoder_1_mo), .CLR(RESET_out),
    .D_OUT(_8_bit_memory_unit_1_d_out));
  program_counter program_counter_1 (
    .D(_8_bit_memory_unit_1_d_out), .CLR(RESET_out), .CLK(and_1_out), .EN(instruction_decoder_1_pcc),
    .LD(and_2_out), .Q(program_counter_1_q));
  instruction_decoder instruction_decoder_1 (
    .IR(_8_bit_memory_unit_1_d_out), .CLK(and_1_out), .CLR(RESET_out), .IRL(instruction_decoder_1_iri),
    .S(instruction_decoder_1_s), .PCC(instruction_decoder_1_pcc), .PCE(instruction_decoder_1_pce),
    .MAI(instruction_decoder_1_mai), .MI(instruction_decoder_1_mi), .MO(instruction_decoder_1_mo),
    .IRI(instruction_decoder_1_iri), .AI(instruction_decoder_1_ai), .AO(instruction_decoder_1_ao),
    .BI(instruction_decoder_1_bi), .BO(instruction_decoder_1_bo), .SO(instruction_decoder_1_so),
    .SUB(instruction_decoder_1_sub), .IRD(instruction_decoder_1_ird), .SPI(instruction_decoder_1_spi),
    .SPO(instruction_decoder_1_spo), .SPC(instruction_decoder_1_spc), .POP(instruction_decoder_1_pop),
    .IN(instruction_decoder_1_in), .OUT(instruction_decoder_1_out));
  assign _8_bit_memory_unit_1_d_out = instruction_decoder_1_pce ? program_counter_1_q : 8'bz;  // Driver driver_1
  Seven_Seg_Hex seven_seg_hex_3 (.d(instruction_decoder_1_s), .dp(1'b0));
  and and_2 (and_2_out, ~instruction_decoder_1_spc, instruction_decoder_1_pop);  // And
  Seven_Seg_Hex seven_seg_hex_4 (.d(program_counter_1_q[7:4]), .dp(1'b0));
  Seven_Seg_Hex seven_seg_hex_5 (.d(program_counter_1_q[3:0]), .dp(1'b0));
  Seven_Seg_Hex seven_seg_hex_6 (.d(A_REG_qd_2), .dp(1'b0));
  and and_3 (and_3_out, instruction_decoder_1_spc, instruction_decoder_1_pop);
  Keyboard keyboard_1 (
    .C(and_1_out), .en(instruction_decoder_1_in), .D({keyboard_1_d, _8_bit_memory_unit_1_d_out}));  // open: av
  Seven_Seg_Hex seven_seg_hex_7 (.d(A_REG_qd), .dp(1'b0));
  _8_bit_register A_REG (
    .D(_8_bit_memory_unit_1_d_out), .ST(instruction_decoder_1_ai), .EN(instruction_decoder_1_ao),
    .CLK(and_1_out), .CLR(RESET_out), .QD({A_REG_qd_2, A_REG_qd}), .Q(_8_bit_memory_unit_1_d_out));
  _8_bit_register B_REG (
    .D(_8_bit_memory_unit_1_d_out), .ST(instruction_decoder_1_bi), .EN(instruction_decoder_1_bo),
    .CLK(and_1_out), .CLR(RESET_out), .QD({B_REG_qd_2, B_REG_qd}), .Q(_8_bit_memory_unit_1_d_out));
  Seven_Seg_Hex seven_seg_hex_8 (.d(B_REG_qd_2), .dp(1'b0));
  _8_bit_alu _8_bit_alu_1 (
    .A_IN({A_REG_qd_2, A_REG_qd}), .SO(instruction_decoder_1_so), .SUB(instruction_decoder_1_sub),
    .B_IN({B_REG_qd_2, B_REG_qd}), .S_OUT(_8_bit_memory_unit_1_d_out), .CARRY(_8_bit_alu_1_carry),
    .ZR(_8_bit_alu_1_zr));  // open: GT, EQ, LT
  Seven_Seg_Hex seven_seg_hex_9 (.d(B_REG_qd), .dp(1'b0));
  stack_register stack_register_1 (
    .D(_8_bit_memory_unit_1_d_out), .SPI(instruction_decoder_1_spi), .CLK(and_1_out), .CLR(RESET_out),
    .SPC(instruction_decoder_1_spc), .POP(and_3_out), .SPO(instruction_decoder_1_spo),
    .Q(_8_bit_memory_unit_1_d_out), .QD(stack_register_1_qd));
  Terminal terminal_1 (.D(_8_bit_memory_unit_1_d_out), .C(and_1_out), .en(instruction_decoder_1_out));
  Seven_Seg_Hex seven_seg_hex_10 (.d(stack_register_1_qd[7:4]), .dp(1'b0));
  Seven_Seg_Hex seven_seg_hex_11 (.d(stack_register_1_qd[3:0]), .dp(1'b0));

  // Notes on the sheet:
  //   SYSCLK: Hz: 20
  //   contents of CTRL ROM (hex, n*v repeats v):
  //   6,31,0,0,0,0,0,0,6,31,6,51,0,0,0,0,6,31,6,14,51,0,0,0,6,31,6,14,111,0,0,0,6,31,6, 51,0,0,0,
  //   0,6,31,6,111,0,0,0,0,6,31,6,15,88,0,0,0,6,31,6,15,208,0,0,0,6,31,440,0,0, 0,0,0,6,31,c40,0,
  //   0,0,0,0,6,31,6,8011,0,0,0,0,6,31,6,15,8010,0,0,0,6,31,2004,4000, 88,0,0,0,6,31,2004,4000,208,
  //   0,0,0,6,31,c000,2004,50,0,0,0,6,31,c000,2004,110,0,0, 0,6,31,6,1011,0,0,0,0,0,0,0,0,0,0,0,0,
  //   6,31,10040,0,0,0,0,0,6,31,10100,0,0,0,0,0,6, 31,20080,0,0,0,0,0,6,31,20200
endmodule
