// Digital circuit flag-unit.dig as structural Verilog
module flag_unit (
  input  [2:0] D,
  input  [4:0] F,
  input  SO,
  input  LD,
  input  CLF
);

  wire decoder_1_out_0, decoder_1_out_1, decoder_1_out_2, decoder_1_out_3, decoder_1_out_4, decoder_1_out_5,
       decoder_1_out_6, decoder_1_out_7;

  Decoder #(.Selector_Bits(3)) decoder_1 (
    .sel(D), .out_0(decoder_1_out_0), .out_1(decoder_1_out_1), .out_2(decoder_1_out_2),
    .out_3(decoder_1_out_3), .out_4(decoder_1_out_4), .out_5(decoder_1_out_5), .out_6(decoder_1_out_6),
    .out_7(decoder_1_out_7));
  _8_bit_register _8_bit_register_1 ();  // open: D, ST, EN, CLK, CLR, QD, Q

  // Notes on the sheet:
  //   D: flag input in
  //   F: load from alu on arithmetic operation
  //   SO: arithmetic operation causes flags to latch from F
  //   LD: loads from D when this line is high
  //   CLF: clears the selected flag when high
endmodule
