// Digital circuit instruction decoder.dig as structural Verilog
module instruction_decoder (
  input  [2:0] S_IN,
  input  [3:0] INSTR_IN,
  input  [2:0] FLAGS_IN,
  output PCC,
  output PCE,
  output IRL,
  output ARL,
  output ARE,
  output MAL,
  output MEL,
  output MEE,
  output JMP,
  output NONE_2
);

  ROM #(.AddrBits(10), .Bits(10)) INSTR_DECODE (
    .A({FLAGS_IN, INSTR_IN, S_IN}), .sel(1'b1), .D({NONE_2, JMP, MEE, MEL, MAL, ARE, ARL, IRL, PCE, PCC}));

  // Notes on the sheet:
  //   S_IN: Step counter in
  //   INSTR_IN: Instruction register in
  //   FLAGS_IN: Flags input
  //   PCC: PC Counter - Count
  //   PCE: Enable Program Counter on the bus
  //   IRL: Load instruction register
  //   ARL: Load argument register
  //   ARE: Enable argument register on the bus
  //   MAL: Load memory address register
  //   MEL: Load a word from the bus into memory
  //   MEE: Place a word from memory on the data bus
  //   JMP: Execute a jump to a new instruction
endmodule
