// Digital circuit instruction-decoder.dig as structural Verilog
module instruction_decoder (
  input  [7:0] IR,
  input  CLK,
  input  CLR,
  input  IRL,
  output [3:0] S,
  output PCC,
  output PCE,
  output MAI,
  output MI,
  output MO,
  output IRI,
  output AI,
  output AO,
  output BI,
  output BO,
  output SO,
  output SUB,
  output [7:0] IRD,
  output SPI,
  output SPO,
  output SPC,
  output POP,
  output IN,
  output OUT
);

  wire not_1_out;

  not not_1 (not_1_out, CLK);
  _8_bit_register _8_bit_register_1 (.D(IR), .ST(IRL), .EN(1'b0), .CLK(CLK), .CLR(CLR), .QD(IRD));  // open: Q
  step_counter STEP (.CLR(CLR), .CLK(not_1_out), .Q(S[2:0]));
  ROM #(.AddrBits(11), .Bits(18)) CTRL_ROM (
    .A({IRD, S[2:0]}), .sel(1'b1),
    .D({OUT, IN, POP, SPC, SPO, SPI, SUB, SO, BO, BI, AO, AI, IRI, MO, MI, MAI, PCE, PCC}));

  assign S[3] = 1'b0;

  // Notes on the sheet:
  //   IR: instruction register input
  //   CLK: clock input
  //   CLR: clear step counter
  //   S: step counter out
  //   IRL: load the instruction register
  //   PCC: program counter count
  //   PCE: enable program counter on the bus
  //   MAI: load memory address register
  //   MI: store data to RAM
  //   MO: output data from memory onto the bus
  //   IRI: load data to instruction register
  //   AI: store data to register A
  //   AO: place register A on the data bus
  //   BI: place data into B register
  //   BO: put register B onto the data bus
  //   SO: enable ALU output on the bus
  //   SUB: subtract
  //   IRD: instruction register out to lcd
  //   SPI: stack pointer input
  //   SPO: stack pointer output
  //   SPC: count stack pointer
  //   POP: set when a value has been pop from the stack
  //   IN: Put value from keyboard input on the bus
  //   OUT: Put a byte from the bus out to the text terminal
  //   contents of CTRL ROM (hex, n*v repeats v):
  //   6,1,0,0,0,0,0,0,6,1,0,0,0,0,0,0,6,1,0,0,0,0,0,0,6,1,0,0,0,0,0,0,6,1,0,0,0,0,0,0,6, 1,0,0,0,
  //   0,0,0,6,1,0,0,0,0,0,0,6,1,0,0,0,0,0,0,6,1,0,0,0,0,0,0,6,1,0,0,0,0,0,0,6,1, 0,0,0,0,0,0,6,1,
  //   0,0,0,0,0,0,6,1,0,0,0,0,0,0,6,1,0,0,0,0,0,0,6,1,0,0,0,0,0,0,6,1
endmodule
