// Digital circuit memory unit.dig as structural Verilog
module memory_unit (
  input  CLK,
  input  MAL,
  input  [3:0] DIN,
  input  MEE,
  input  MEL,
  output [3:0] DOUT
);

  wire and_1_out;
  wire [3:0] MAR_q;

  Register #(.Bits(4)) MAR (.D(DIN), .C(CLK), .en(MAL), .Q(MAR_q));
  and and_1 (and_1_out, CLK, MEL);
  RAMSinglePortSel #(.AddrBits(4), .isProgramMemory("true"), .Bits(4)) RAM (
    .A(MAR_q), .CS(1'b1), .WE(and_1_out), .OE(MEE), .D(DIN));

  assign DOUT = DIN;

  // Notes on the sheet:
  //   CLK: Clock input
  //   MAL: Load memory address register from the bus
  //   DIN: Data bus input
  //   MEE: Enable memory on the bus
  //   MEL: Load memory from the bus
  //   DOUT: Data bus out
endmodule
