// Digital circuit program counter.dig as structural Verilog
module program_counter (
  input  CLR,
  input  CLK,
  input  [3:0] DIN,
  input  JMP,
  input  PCC,
  input  PCE,
  input  IRL,
  input  ARL,
  input  ARE,
  output [2:0] STEP,
  output [3:0] DOUT,
  output [3:0] IOUT
);

  wire not_1_out;
  wire [3:0] DR_q, PC_out;

  not not_1 (not_1_out, 1'b1);
  Counter #(.Bits(3)) u_STEP (.en(1'b1), .C(CLK), .clr(CLR), .out(STEP));  // open: ovf
  CounterPreset #(.maxValue(16), .Bits(4)) PC (
    .en(PCC), .C(CLK), .dir(not_1_out), .in(DIN), .ld(JMP), .clr(CLR), .out(PC_out));  // open: ovf
  Register #(.Bits(4)) IR (.D(DIN), .C(CLK), .en(IRL), .Q(IOUT));
  Register #(.Bits(4)) DR (.D(DIN), .C(CLK), .en(ARL), .Q(DR_q));
  assign DOUT = PCE ? PC_out : 4'bz;  // Driver driver_1
  assign DOUT = ARE ? DR_q : 4'bz;  // Driver driver_2

  // Notes on the sheet:
  //   PCC: Count
  //   PCE: Enable program counter on the bus
  //   IRL: Load instruction register
  //   ARL: Load argument register
  //   ARE: Enable the argument register on the bus
endmodule
