// Digital circuit program-counter.dig as structural Verilog
module program_counter (
  input  [7:0] D,
  input  CLR,
  input  CLK,
  input  EN,
  input  LD,
  output [7:0] Q
);

  wire _4_bit_counter_with_load_clear_1_c;

  _4_bit_counter_with_load_clear _4_bit_counter_with_load_clear_1 (
    .LD(LD), .EN(EN), .D_IN(D[3:0]), .CLR(CLR), .CLK(CLK), .D_OUT(Q[3:0]),
    .C(_4_bit_counter_with_load_clear_1_c));
  _4_bit_counter_with_load_clear _4_bit_counter_with_load_clear_2 (
    .LD(LD), .EN(_4_bit_counter_with_load_clear_1_c), .D_IN(D[7:4]), .CLR(CLR), .CLK(CLK), .D_OUT(Q[7:4]));  // open: C

  // Notes on the sheet:
  //   D: data input
  //   CLR: resets counter to 0 asynchronously
  //   CLK: clock input
  //   EN: when high, counter will increment on clock pulse
  //   LD: when high, counter loads from input on next clock pulse
  //   Q: output of counter
endmodule
