// Digital circuit stack-register.dig as structural Verilog
module stack_register (
  input  [7:0] D,
  input  SPI,
  input  CLK,
  input  CLR,
  input  SPC,
  input  POP,
  input  SPO,
  output [7:0] Q,
  output [7:0] QD
);

  wire not_1_out;

  not not_1 (not_1_out, POP);
  CounterPreset #(.Bits(8)) counterpreset_1 (
    .en(SPC), .C(CLK), .dir(not_1_out), .in(D), .ld(SPI), .clr(CLR), .out(QD));  // open: ovf
  assign Q = SPO ? QD : 8'bz;  // Driver driver_1

  // Notes on the sheet:
  //   Q: data output
  //   D: data input
  //   SPI: load the stack pointer
  //   CLK: clock input
  //   CLR: clear the stack pointer
  //   SPC: stack pointer count
  //   POP: when high, counter will increment
  //   SPO: put the stack pointer on the data bus when high
  //   QD: output for display
endmodule
