// Digital circuit step-counter.dig as structural Verilog
module step_counter (
  input  CLR,
  input  CLK,
  output [2:0] Q
);

  wire _1_bit_counter_with_load_clear_1_c, _1_bit_counter_with_load_clear_2_c, not_1_out;

  not not_1 (not_1_out, 1'b0);
  _1_bit_counter_with_load_clear _1_bit_counter_with_load_clear_1 (
    .LD(1'b0), .EN(not_1_out), .D(1'b0), .CLR(CLR), .CLK(CLK), .Q(Q[0]),
    .C(_1_bit_counter_with_load_clear_1_c));
  _1_bit_counter_with_load_clear _1_bit_counter_with_load_clear_2 (
    .LD(1'b0), .EN(_1_bit_counter_with_load_clear_1_c), .D(1'b0), .CLR(CLR), .CLK(CLK), .Q(Q[1]),
    .C(_1_bit_counter_with_load_clear_2_c));
  _1_bit_counter_with_load_clear _1_bit_counter_with_load_clear_3 (
    .LD(1'b0), .EN(_1_bit_counter_with_load_clear_2_c), .D(1'b0), .CLR(CLR), .CLK(CLK), .Q(Q[2]));  // open: C

  // Notes on the sheet:
  //   CLR: when high, asynchronously clears counter
  //   CLK: clock input
  //   Q: counter output
endmodule
